// Digital circuit 1-bit-full-adder.dig as structural Verilog
module _1_bit_full_adder (
  input  a,
  input  b,
  input  cin,
  output sum,
  output cout
);

  Add add_1 (.a(a), .b(b), .c_i(cin), .s(sum), .c_o(cout));
endmodule
