// Digital circuit 32-bit-eq.dig as structural Verilog
module _32_bit_eq (
  input  [31:0] A,
  input  [31:0] B,
  output EQ
);

  wire _4_bit_eq_1_eq, _7_bit_eq_1_eq, _7_bit_eq_2_eq, _7_bit_eq_3_eq, _7_bit_eq_4_eq;

  _7_bit_eq _7_bit_eq_1 (.A(A[6:0]), .B(B[6:0]), .EQ(_7_bit_eq_1_eq));
  _7_bit_eq _7_bit_eq_2 (.A(A[13:7]), .B(B[13:7]), .EQ(_7_bit_eq_2_eq));
  _7_bit_eq _7_bit_eq_3 (.A(A[20:14]), .B(B[20:14]), .EQ(_7_bit_eq_3_eq));
  _7_bit_eq _7_bit_eq_4 (.A(A[27:21]), .B(B[27:21]), .EQ(_7_bit_eq_4_eq));
  _4_bit_eq _4_bit_eq_1 (.A(A[31:28]), .B(B[31:28]), .EQ(_4_bit_eq_1_eq));
  and and_1 (EQ, _7_bit_eq_1_eq, _7_bit_eq_2_eq, _7_bit_eq_3_eq, _7_bit_eq_4_eq, _4_bit_eq_1_eq);
endmodule
