// Digital circuit 5-bit-eq.dig as structural Verilog
module _5_bit_eq (
  input  [4:0] A,
  input  [4:0] B,
  output EQ
);

  wire xnor_1_out, xnor_2_out, xnor_3_out, xnor_4_out, xnor_5_out;

  xnor xnor_1 (xnor_1_out, A[0], B[0]);
  xnor xnor_2 (xnor_2_out, A[1], B[1]);
  xnor xnor_3 (xnor_3_out, A[2], B[2]);
  xnor xnor_4 (xnor_4_out, A[3], B[3]);
  xnor xnor_5 (xnor_5_out, A[4], B[4]);
  and and_1 (EQ, xnor_1_out, xnor_2_out, xnor_3_out, xnor_4_out, xnor_5_out);
endmodule
