// Digital circuit 64-bit-register.dig as structural Verilog
module _64_bit_register (
  input  [63:0] D,
  input  CLR,
  input  EN,
  input  CLK,
  output [63:0] Q
);

  _8_bit_register _8_bit_register_1 (.D(D[7:0]), .CLK(CLK), .EN(EN), .CLR(CLR), .Q(Q[7:0]));
  _8_bit_register _8_bit_register_2 (.D(D[15:8]), .CLK(CLK), .EN(EN), .CLR(CLR), .Q(Q[15:8]));
  _8_bit_register _8_bit_register_3 (.D(D[23:16]), .CLK(CLK), .EN(EN), .CLR(CLR), .Q(Q[23:16]));
  _8_bit_register _8_bit_register_4 (.D(D[31:24]), .CLK(CLK), .EN(EN), .CLR(CLR), .Q(Q[31:24]));
  _8_bit_register _8_bit_register_5 (.D(D[39:32]), .CLK(CLK), .EN(EN), .CLR(CLR), .Q(Q[39:32]));
  _8_bit_register _8_bit_register_6 (.D(D[47:40]), .CLK(CLK), .EN(EN), .CLR(CLR), .Q(Q[47:40]));
  _8_bit_register _8_bit_register_7 (.D(D[55:48]), .CLK(CLK), .EN(EN), .CLR(CLR), .Q(Q[55:48]));
  _8_bit_register _8_bit_register_8 (.D(D[63:56]), .CLK(CLK), .EN(EN), .CLR(CLR), .Q(Q[63:56]));
endmodule
