// Digital circuit 8-bit-counter.dig as structural Verilog
module _8_bit_counter (
  input  CLK,
  input  CLR,
  output [7:0] COUNTER
);

  wire [7:0] _8_bit_adder_1_sum;

  _8_bit_register _8_bit_register_1 (.D(_8_bit_adder_1_sum), .CLK(CLK), .EN(1'b1), .CLR(CLR), .Q(COUNTER));
  _8_bit_adder _8_bit_adder_1 (.A(COUNTER), .B(8'h1), .sum(_8_bit_adder_1_sum));  // open: COUT
endmodule
