// Digital circuit 8-bit-register.dig as structural Verilog
module _8_bit_register (
  input  [7:0] D,
  input  CLK,
  input  EN,
  input  CLR,
  output [7:0] Q
);

  d_flip_flop d_flip_flop_1 (.CLK(CLK), .D(D[0]), .EN(EN), .CLR(CLR), .Q(Q[0]));
  d_flip_flop d_flip_flop_2 (.CLK(CLK), .D(D[1]), .EN(EN), .CLR(CLR), .Q(Q[1]));
  d_flip_flop d_flip_flop_3 (.CLK(CLK), .D(D[2]), .EN(EN), .CLR(CLR), .Q(Q[2]));
  d_flip_flop d_flip_flop_4 (.CLK(CLK), .D(D[3]), .EN(EN), .CLR(CLR), .Q(Q[3]));
  d_flip_flop d_flip_flop_5 (.CLK(CLK), .D(D[4]), .EN(EN), .CLR(CLR), .Q(Q[4]));
  d_flip_flop d_flip_flop_6 (.CLK(CLK), .D(D[5]), .EN(EN), .CLR(CLR), .Q(Q[5]));
  d_flip_flop d_flip_flop_7 (.CLK(CLK), .D(D[6]), .EN(EN), .CLR(CLR), .Q(Q[6]));
  d_flip_flop d_flip_flop_8 (.CLK(CLK), .D(D[7]), .EN(EN), .CLR(CLR), .Q(Q[7]));
endmodule
