// Digital circuit ADDIW.dig as structural Verilog
module ADDIW (
  input  [6:0] iw_opcode,
  input  [6:0] opcode,
  input  [2:0] iw_funct3,
  input  [2:0] funct3,
  output eq
);

  wire add_eq, i_type_eq;

  Comparator #(.Bits(7)) i_type (.a(iw_opcode), .b(opcode), .eq(i_type_eq));  // open: gt, lt
  Comparator #(.Bits(3)) add (.a(iw_funct3), .b(funct3), .eq(add_eq));  // open: gt, lt
  and and_1 (eq, i_type_eq, add_eq);
endmodule
