// Digital circuit InstDecoder2.dig as structural Verilog
module InstDecoder2 (
  input  [31:0] IW,
  output [2:0] ALUSrcB,
  output [3:0] ALUOp,
  output RFW,
  output ALUSrcA,
  output WDsel,
  output PCsel,
  output [2:0] BROp,
  output [1:0] size,
  output MR,
  output store,
  output load
);

  wire addi_1_eq, addiw_1_eq, addr_1_eq, and_1_eq, beq_1_eq, bge_1_eq, blt_1_eq, bne_1_eq, jal_eq, jalr_1_eq,
       lb_1_eq, LD_eq, lui_eq, LW_eq, mul_1_eq, or_1_eq, SB_eq, SD_eq, slli_1_p7, sllr_1_eq, srli_1_eq,
       srlr_1_eq, sub_1_eq, subw_1_eq, SW_eq;
  wire [4:0] INUM_num;

  ADDI addi_1 (.eq(addi_1_eq), .iw_opcode(IW[6:0]), .opcode(7'b0010011), .iw_funct3(IW[14:12]), .funct3(3'b000));
  ADDR addr_1 (
    .iw_opcode(IW[6:0]), .opcode(7'b0110011), .iw_funct3(IW[14:12]), .funct3(3'b000), .iw_funct7(IW[31:25]),
    .funct7({7{1'b0}}), .eq(addr_1_eq));
  Comparator #(.Bits(7)) jal (.a(IW[6:0]), .b(7'b1101111), .eq(jal_eq));  // open: gt, lt
  JALR jalr_1 (.eq(jalr_1_eq), .iw_opcode(IW[6:0]), .opcode(7'b1100111), .iw_funct3(IW[14:12]), .funct3(3'b000));
  SLLR sllr_1 (
    .iw_opcode(IW[6:0]), .opcode(7'b0110011), .iw_funct3(IW[14:12]), .funct3(3'b001), .iw_funct7(IW[31:25]),
    .funct7({7{1'b0}}), .eq(sllr_1_eq));
  // SLLI slli_1: pin names not known; wires that end beside it: IW[6:0], 7'b0010011, IW[14:12], 3'b001, IW[31:26], {6{1'b0}}, slli_1_p7
  SRLR srlr_1 (
    .iw_opcode(IW[6:0]), .opcode(7'b0110011), .iw_funct3(IW[14:12]), .funct3(3'b101), .iw_funct7(IW[31:25]),
    .funct7({7{1'b0}}), .eq(srlr_1_eq));
  SRLI srli_1 (
    .iw_opcode(IW[6:0]), .opcode(7'b0010011), .iw_funct3(IW[14:12]), .funct3(3'b101), .iw_funct6(IW[31:26]),
    .funct6({6{1'b0}}), .eq(srli_1_eq));
  beq beq_1 (.iw_opcode(IW[6:0]), .opcode(7'b1100011), .iw_funct3(IW[14:12]), .funct3(3'b000), .eq(beq_1_eq));
  bne bne_1 (.iw_opcode(IW[6:0]), .opcode(7'b1100011), .iw_funct3(IW[14:12]), .funct3(3'b001), .eq(bne_1_eq));
  blt blt_1 (.iw_opcode(IW[6:0]), .opcode(7'b1100011), .iw_funct3(IW[14:12]), .funct3(3'b100), .eq(blt_1_eq));
  bge bge_1 (.iw_opcode(IW[6:0]), .opcode(7'b1100011), .iw_funct3(IW[14:12]), .funct3(3'b101), .eq(bge_1_eq));
  MUL mul_1 (
    .iw_opcode(IW[6:0]), .opcode(7'b0110011), .iw_funct3(IW[14:12]), .funct3(3'b000), .iw_funct7(IW[31:25]),
    .funct7(7'b0000001), .eq(mul_1_eq));
  SUB sub_1 (
    .iw_opcode(IW[6:0]), .opcode(7'b0110011), .iw_funct3(IW[14:12]), .funct3(3'b000), .iw_funct7(IW[31:25]),
    .funct7(7'b0100000), .eq(sub_1_eq));
  LB lb_1 (.eq(lb_1_eq), .iw_opcode(IW[6:0]), .opcode(7'b0000011), .iw_funct3(IW[14:12]), .funct3(3'b000));
  LB LW (.eq(LW_eq), .iw_opcode(IW[6:0]), .opcode(7'b0000011), .iw_funct3(IW[14:12]), .funct3(3'b010));
  LB SB (.eq(SB_eq), .iw_opcode(IW[6:0]), .opcode(7'b0100011), .iw_funct3(IW[14:12]), .funct3(3'b000));
  LB SW (.eq(SW_eq), .iw_opcode(IW[6:0]), .opcode(7'b0100011), .iw_funct3(IW[14:12]), .funct3(3'b010));
  AND and_1 (
    .iw_opcode(IW[6:0]), .opcode(7'b0110011), .iw_funct3(IW[14:12]), .funct3(3'b111), .iw_funct7(IW[31:25]),
    .funct7({7{1'b0}}), .eq(and_1_eq));
  OR or_1 (
    .iw_opcode(IW[6:0]), .opcode(7'b0110011), .iw_funct3(IW[14:12]), .funct3(3'b110), .iw_funct7(IW[31:25]),
    .funct7({7{1'b0}}), .eq(or_1_eq));
  LB LD (.eq(LD_eq), .iw_opcode(IW[6:0]), .opcode(7'b0000011), .iw_funct3(IW[14:12]), .funct3(3'b011));
  LB SD (.eq(SD_eq), .iw_opcode(IW[6:0]), .opcode(7'b0100011), .iw_funct3(IW[14:12]), .funct3(3'b011));
  ADDIW addiw_1 (.eq(addiw_1_eq), .iw_opcode(IW[6:0]), .opcode(7'b0011011), .iw_funct3(IW[14:12]), .funct3(3'b000));
  SUBW subw_1 (
    .iw_opcode(IW[6:0]), .opcode(7'b0111011), .iw_funct3(IW[14:12]), .funct3(3'b000), .iw_funct7(IW[31:25]),
    .funct7(7'b0100000), .eq(subw_1_eq));
  Comparator #(.Bits(7)) lui (.a(IW[6:0]), .b(7'b0110111), .eq(lui_eq));  // open: gt, lt
  PriorityEncoder #(.Selector_Bits(5)) INUM (
    .in0(addi_1_eq), .in1(addr_1_eq), .in2(jal_eq), .in3(jalr_1_eq), .in4(sllr_1_eq), .in5(slli_1_p7),
    .in6(srlr_1_eq), .in7(srli_1_eq), .in8(beq_1_eq), .in9(bne_1_eq), .in10(blt_1_eq), .in11(bge_1_eq),
    .in12(mul_1_eq), .in13(sub_1_eq), .in14(lui_eq), .in15(lb_1_eq), .in16(LW_eq), .in17(SB_eq),
    .in18(SW_eq), .in19(and_1_eq), .in20(or_1_eq), .in21(LD_eq), .in22(SD_eq), .in23(addiw_1_eq),
    .in24(subw_1_eq), .in25(1'b0), .in26(1'b0), .in27(1'b0), .in28(1'b0), .in29(1'b0), .in30(1'b0),
    .in31(1'b0), .num(INUM_num));  // open: any
  ROM #(.AddrBits(5), .Bits(19)) rom_1 (
    .A(INUM_num), .sel(1'b1), .D({RFW, ALUOp, ALUSrcA, ALUSrcB, PCsel, WDsel, BROp, size, MR, store, load}));

  // Other names for the same wires on the sheet: opcode[6:0] = IW[6:0]; funct3[2:0] = IW[14:12];
  //   funct7[6:0] = IW[31:25]; funct6[5:0] = IW[31:26]

  // Notes on the sheet:
  //   contents of rom_1 (hex, n*v repeats v):
  //   40400,40000,43700,700,50000,51800,54000,55800,2c20,2c40,2c80,2c60
  //   ,48000,44000,6d000,4040d,40415,90b,913,60000,64000,4041d,91b,68400
endmodule
