// Digital circuit SRLR.dig as structural Verilog
module SRLR (
  input  [6:0] iw_opcode,
  input  [6:0] opcode,
  input  [2:0] iw_funct3,
  input  [2:0] funct3,
  input  [6:0] iw_funct7,
  input  [6:0] funct7,
  output eq
);

  wire comparator_1_eq, comparator_2_eq, comparator_3_eq;

  Comparator #(.Bits(7)) comparator_1 (.a(iw_opcode), .b(opcode), .eq(comparator_1_eq));  // open: gt, lt
  Comparator #(.Bits(3)) comparator_2 (.a(iw_funct3), .b(funct3), .eq(comparator_2_eq));  // open: gt, lt
  Comparator #(.Bits(7)) comparator_3 (.a(iw_funct7), .b(funct7), .eq(comparator_3_eq));  // open: gt, lt
  and and_1 (eq, comparator_1_eq, comparator_2_eq, comparator_3_eq);
endmodule
