// Digital circuit alu.dig as structural Verilog
module alu (
  input  [63:0] A,
  input  [63:0] B,
  input  [3:0] ALUOp,
  output [63:0] R
);

  wire [31:0] add_2_s;
  wire [63:0] add_1_s, and_1_out, barrelshifter_1_out, barrelshifter_2_out, barrelshifter_3_out,
       barrelshifter_4_out, bitextender_1_out, div_1_r, mul_1_mul, or_1_out, sub_1_s;

  Add #(.Bits(64)) add_1 (.a(A), .b(B), .c_i(1'b0), .s(add_1_s));  // open: c_o
  Sub #(.Bits(64)) sub_1 (.a(A), .b(B), .c_i(1'b0), .s(sub_1_s));  // open: c_o
  Mul #(.Bits(32)) mul_1 (.a(A[31:0]), .b(B[31:0]), .mul(mul_1_mul));
  Div #(.Bits(64)) div_1 (.a(A), .b(B), .r(div_1_r));  // open: q
  BarrelShifter #(.Bits(64)) barrelshifter_1 (.in(A), .shift(B[6:0]), .out(barrelshifter_1_out));
  BarrelShifter #(.Bits(64), .direction("right")) barrelshifter_2 (.in(A), .shift(B[6:0]), .out(barrelshifter_2_out));
  BarrelShifter #(.Bits(64), .barrelShifterMode("arithmetic")) barrelshifter_3 (
    .in(A), .shift(B[6:0]), .out(barrelshifter_3_out));
  BarrelShifter #(.Bits(64), .barrelShifterMode("arithmetic"), .direction("right")) barrelshifter_4 (
    .in(A), .shift(B[6:0]), .out(barrelshifter_4_out));
  assign and_1_out = A & B;  // And and_1, 64 bits wide
  assign or_1_out = A | B;  // Or or_1, 64 bits wide
  Add #(.Bits(32)) add_2 (.a(A[31:0]), .b(B[31:0]), .c_i(1'b0), .s(add_2_s));  // open: c_o
  BitExtender #(.inputBits(32), .outputBits(64)) bitextender_1 (.in(add_2_s), .out(bitextender_1_out));
  Multiplexer #(.Selector_Bits(4), .Bits(64)) multiplexer_1 (
    .sel(ALUOp), .in_0(add_1_s), .in_1(sub_1_s), .in_2(mul_1_mul), .in_3(div_1_r),
    .in_4(barrelshifter_1_out), .in_5(barrelshifter_2_out), .in_6(barrelshifter_3_out),
    .in_7(barrelshifter_4_out), .in_8(and_1_out), .in_9(or_1_out), .in_10(bitextender_1_out), .in_11(B),
    .in_12({64{1'b0}}), .in_13({64{1'b0}}), .in_14({64{1'b0}}), .in_15({64{1'b0}}), .out(R));
endmodule
