// Digital circuit analyze-decoder.dig as structural Verilog
module analyze_decoder (
  input  [31:0] IW,
  output [2:0] INUM
);

  wire _5_bit_eq_1_eq, and_1_out, B_TYPE_eq, I_TYPE_eq, J_eq, JAL_eq, JALR_eq, LOAD_eq, R_TYPE_eq, S_TYPE_eq;

  _7_bit_eq I_TYPE (.A(IW[6:0]), .B(7'b0010011), .EQ(I_TYPE_eq));
  _7_bit_eq R_TYPE (.A(IW[6:0]), .B(7'b0110011), .EQ(R_TYPE_eq));
  _7_bit_eq LOAD (.A(IW[6:0]), .B(7'b0000011), .EQ(LOAD_eq));
  _7_bit_eq S_TYPE (.A(IW[6:0]), .B(7'b0100011), .EQ(S_TYPE_eq));
  _7_bit_eq B_TYPE (.A(IW[6:0]), .B(7'b1100011), .EQ(B_TYPE_eq));
  _7_bit_eq JAL (.A(IW[6:0]), .B(7'b1101111), .EQ(JAL_eq));
  _7_bit_eq J (.A(IW[6:0]), .B(7'b1101111), .EQ(J_eq));
  _5_bit_eq _5_bit_eq_1 (.A(IW[11:7]), .B({5{1'b0}}), .EQ(_5_bit_eq_1_eq));
  _7_bit_eq JALR (.A(IW[6:0]), .B(7'b1100111), .EQ(JALR_eq));
  and and_1 (and_1_out, J_eq, _5_bit_eq_1_eq);
  PriorityEncoder #(.Selector_Bits(3)) priorityencoder_1 (
    .in0(I_TYPE_eq), .in1(R_TYPE_eq), .in2(LOAD_eq), .in3(S_TYPE_eq), .in4(B_TYPE_eq), .in5(JAL_eq),
    .in6(and_1_out), .in7(JALR_eq), .num(INUM));  // open: any
endmodule
