// Digital circuit d-latch.dig as structural Verilog
module d_latch (
  input  D,
  input  CLK,
  output Q,
  output notQ
);

  wire and_1_out, and_2_out;

  and and_1 (and_1_out, CLK, ~D);  // And
  and and_2 (and_2_out, CLK, D);
  // sr_latch sr_latch_1: pin names not known; wires that end beside it: and_1_out, and_2_out, Q, notQ
endmodule
