// Digital circuit instruction_memeory.dig as structural Verilog
module instruction_memeory (
  input  [7:0] ADDR,
  input  [1:0] PROG,
  output [31:0] IW
);

  wire [31:0] part1_d, part2_d;

  ROM #(.AddrBits(8), .Bits(32)) part1 (.A(ADDR), .sel(1'b1), .D(part1_d));
  ROM #(.AddrBits(8), .Bits(32)) part2 (.A(ADDR), .sel(1'b1), .D(part2_d));
  Multiplexer #(.Selector_Bits(2), .Bits(32)) multiplexer_1 (
    .sel(PROG), .in_0(part1_d), .in_1(part2_d), .in_2({32{1'b0}}), .in_3({32{1'b0}}), .out(IW));

  // Notes on the sheet:
  //   contents of part1 (hex, n*v repeats v):
  //   100513,200593,b50633,c0001073
  //   contents of part2 (hex, n*v repeats v):
  //   100513,200593,8000ef,c0001073,b50533,8067
endmodule
