// Digital circuit project06.dig as structural Verilog
module project06 (
  input  CLK,
  input  EN,
  input  CLR,
  input  [4:0] PROG,
  output [63:0] A0,
  output [63:0] A1,
  output [63:0] A2,
  output DONE,
  output [63:0] zero,
  output [63:0] ra,
  output [63:0] sp,
  output [63:0] gp,
  output [63:0] tp,
  output [63:0] t0,
  output [63:0] t1,
  output [63:0] t2,
  output [63:0] s0_fp,
  output [63:0] s1,
  output [63:0] a0_2,
  output [63:0] a1_2,
  output [63:0] a2_2,
  output [63:0] a3,
  output [63:0] a4,
  output [63:0] a5,
  output [63:0] a6,
  output [63:0] a7,
  output [63:0] s2,
  output [63:0] s3,
  output [63:0] s4,
  output [63:0] s5,
  output [63:0] s6,
  output [63:0] s7,
  output [63:0] s8,
  output [63:0] s9,
  output [63:0] s10,
  output [63:0] s11,
  output [63:0] t3,
  output [63:0] t4,
  output [63:0] t5,
  output [63:0] t6
);

  wire ALUSrcA, and_2_out, CLK_t, load, MR, PCBr, PCsel, RFW, store, WDsel;
  wire [1:0] sz;
  wire [2:0] ALUSrcB, BROp;
  wire [3:0] ALUOp;
  wire [4:0] rd, rs1, rs2;
  wire [31:0] iw;
  wire [63:0] alu_1_r, imm_I, immdecoder_1_imm_b, immdecoder_1_imm_j, immdecoder_1_imm_s, immdecoder_1_imm_u,
       immdecoder_1_shift, loads_read_dout, multiplexer_1_out, multiplexer_2_out, multiplexer_3_out,
       multiplexer_4_out, multiplexer_5_out, PC, PC_plus_4, ramdualport_1_d, register_file_1_rd0,
       register_file_1_rd1, stores_write_dout;

  Multiplexer #(.Bits(64)) multiplexer_1 (
    .sel(PCBr), .in_0(PC_plus_4), .in_1(multiplexer_5_out), .out(multiplexer_1_out));
  _64_bit_register2 _64_bit_register2_1 (.D(multiplexer_1_out), .CLK(CLK_t), .EN(EN), .CLR(CLR), .Q(PC));
  and and_1 (CLK_t, CLK, ~DONE);  // And
  Comparator #(.Bits(32)) END (.a(iw), .b(32'hc0001073), .eq(DONE));  // open: gt, lt
  LED led_1 (.in(DONE));
  // inst_mem inst_mem_1: pin names not known; wires that end beside it: PROG, PC[9:2], iw
  Add #(.Bits(64)) u_PC_plus_4 (.a(PC), .b(64'h4), .c_i(1'b0), .s(PC_plus_4));  // open: c_o
  InstDecoder2 instdecoder2_1 (
    .IW(iw), .load(load), .store(store), .MR(MR), .size(sz), .BROp(BROp), .WDsel(WDsel), .PCsel(PCsel),
    .ALUSrcB(ALUSrcB), .ALUSrcA(ALUSrcA), .ALUOp(ALUOp), .RFW(RFW));
  RegDecoder regdecoder_1 (.IW(iw), .RS1(rs1), .RS2(rs2), .RD(rd));
  ImmDecoder immdecoder_1 (
    .IW(iw), .imm_I(imm_I), .imm_S(immdecoder_1_imm_s), .imm_B(immdecoder_1_imm_b),
    .imm_U(immdecoder_1_imm_u), .imm_J(immdecoder_1_imm_j), .Shift(immdecoder_1_shift));
  // Probe on PC
  // Probe on iw
  // Probe on rs1
  // Probe on rs2
  // Probe on rd
  // Probe on imm_I
  Multiplexer #(.Bits(64)) multiplexer_2 (
    .sel(WDsel), .in_0(multiplexer_5_out), .in_1(PC_plus_4), .out(multiplexer_2_out));
  and and_2 (and_2_out, RFW, EN);
  register_file register_file_1 (
    .ReadReg0(rs1), .ReadReg1(rs2), .WriteData(multiplexer_2_out), .WriteEn(and_2_out), .WriteReg(rd),
    .CLK(CLK_t), .CLR(CLR), .RD0(register_file_1_rd0), .RD1(register_file_1_rd1), .x0(zero), .x1(ra),
    .x2(sp), .x3(gp), .x4(tp), .x5(t0), .x6(t1), .x7(t2), .x8(s0_fp), .x9(s1), .x10(A0), .x11(A1), .x12(A2),
    .x13(a3), .x14(a4), .x15(a5), .x16(a6), .x17(a7), .x18(s2), .x19(s3), .x20(s4), .x21(s5), .x22(s6),
    .x23(s7), .x24(s8), .x25(s9), .x26(s10), .x27(s11), .x28(t3), .x29(t4), .x30(t5), .x31(t6));
  Multiplexer #(.Bits(64)) multiplexer_3 (
    .sel(ALUSrcA), .in_0(register_file_1_rd0), .in_1(PC), .out(multiplexer_3_out));
  Multiplexer #(.Selector_Bits(3), .Bits(64)) multiplexer_4 (
    .sel(ALUSrcB), .in_0(register_file_1_rd1), .in_1(imm_I), .in_2(immdecoder_1_imm_s),
    .in_3(immdecoder_1_imm_b), .in_4(immdecoder_1_imm_u), .in_5(immdecoder_1_imm_j),
    .in_6(immdecoder_1_shift), .in_7({64{1'b0}}), .out(multiplexer_4_out));
  bcu bcu_1 (.PCSel(PCsel), .BRop(BROp), .A(register_file_1_rd0), .B(register_file_1_rd1), .PCbr(PCBr));
  alu alu_1 (.A(multiplexer_3_out), .B(multiplexer_4_out), .ALUOp(ALUOp), .R(alu_1_r));
  Multiplexer #(.Bits(64)) multiplexer_5 (.sel(MR), .in_0(alu_1_r), .in_1(loads_read_dout), .out(multiplexer_5_out));
  write stores_write (
    .addr(alu_1_r), .bnew(register_file_1_rd1), .Dcur(ramdualport_1_d), .SZ(sz), .Dout(stores_write_dout));
  RAMDualPort #(.AddrBits(7), .Bits(64)) ramdualport_1 (
    .A(alu_1_r[9:3]), .Din(stores_write_dout), .str(store), .C(CLK_t), .ld(load), .D(ramdualport_1_d));
  read loads_read (.addr(alu_1_r), .Din(ramdualport_1_d), .sz(sz), .Dout(loads_read_dout));

  assign a0_2 = A0;
  assign a1_2 = A1;
  assign a2_2 = A2;

  // Other names for the same wires on the sheet: x0[63:0] = zero; x1[63:0] = ra; x2[63:0] = sp; x3[63:0] = gp;
  //   x4[63:0] = tp; x5[63:0] = t0; x6[63:0] = t1; x7[63:0] = t2; x8[63:0] = s0_fp; x9[63:0] = s1; x10[63:0] = A0;
  //   x11[63:0] = A1; x12[63:0] = A2; x13[63:0] = a3; x14[63:0] = a4; x15[63:0] = a5; x16[63:0] = a6; x17[63:0] = a7;
  //   x18[63:0] = s2; x19[63:0] = s3; x20[63:0] = s4; x21[63:0] = s5; x22[63:0] = s6; x23[63:0] = s7; x24[63:0] = s8;
  //   x25[63:0] = s9; x26[63:0] = s10; x27[63:0] = s11; x28[63:0] = t3; x29[63:0] = t4; x30[63:0] = t5;
  //   x31[63:0] = t6
endmodule
