// Digital circuit read.dig as structural Verilog
module read (
  input  [63:0] addr,
  input  [63:0] Din,
  input  [1:0] sz,
  output [63:0] Dout
);

  wire [7:0] multiplexer_1_out;
  wire [31:0] multiplexer_2_out;
  wire [63:0] bitextender_1_out, bitextender_2_out;

  Multiplexer #(.Selector_Bits(3), .Bits(8)) multiplexer_1 (
    .sel(addr[2:0]), .in_0(Din[7:0]), .in_1(Din[15:8]), .in_2(Din[23:16]), .in_3(Din[31:24]),
    .in_4(Din[39:32]), .in_5(Din[47:40]), .in_6(Din[55:48]), .in_7(Din[63:56]), .out(multiplexer_1_out));
  Multiplexer #(.Bits(32)) multiplexer_2 (.sel(addr[2]), .in_0(Din[31:0]), .in_1(Din[63:32]), .out(multiplexer_2_out));
  BitExtender #(.inputBits(32), .outputBits(64)) bitextender_1 (.in(multiplexer_2_out), .out(bitextender_1_out));
  BitExtender #(.outputBits(64)) bitextender_2 (.in(multiplexer_1_out), .out(bitextender_2_out));
  Multiplexer #(.Selector_Bits(2), .Bits(64)) multiplexer_3 (
    .sel(sz), .in_0({64{1'b0}}), .in_1(bitextender_2_out), .in_2(bitextender_1_out), .in_3(Din), .out(Dout));

  // Other names for the same wires on the sheet: b0[7:0] = Din[7:0]; b1[7:0] = Din[15:8]; b2[7:0] = Din[23:16];
  //   b3[7:0] = Din[31:24]; b4[7:0] = Din[39:32]; b5[7:0] = Din[47:40]; b6[7:0] = Din[55:48]; b7[7:0] = Din[63:56]
endmodule
