// Digital circuit register_file.dig as structural Verilog
module register_file (
  input  [4:0] ReadReg0,
  input  [4:0] ReadReg1,
  input  [4:0] WriteReg,
  input  [63:0] WriteData,
  input  WriteEn,
  input  CLK,
  input  CLR,
  output [63:0] RD0,
  output [63:0] RD1,
  output [63:0] x0,
  output [63:0] x1,
  output [63:0] x2,
  output [63:0] x3,
  output [63:0] x4,
  output [63:0] x5,
  output [63:0] x6,
  output [63:0] x7,
  output [63:0] x8,
  output [63:0] x9,
  output [63:0] x10,
  output [63:0] x11,
  output [63:0] x12,
  output [63:0] x13,
  output [63:0] x14,
  output [63:0] x15,
  output [63:0] x16,
  output [63:0] x17,
  output [63:0] x18,
  output [63:0] x19,
  output [63:0] x20,
  output [63:0] x21,
  output [63:0] x22,
  output [63:0] x23,
  output [63:0] x24,
  output [63:0] x25,
  output [63:0] x26,
  output [63:0] x27,
  output [63:0] x28,
  output [63:0] x29,
  output [63:0] x30,
  output [63:0] x31
);

  wire and_1_out, and_2_out, and_3_out, and_4_out, and_5_out, and_6_out, and_7_out, and_8_out, and_9_out,
       and_10_out, and_11_out, and_12_out, and_13_out, and_14_out, and_15_out, and_16_out, and_17_out,
       and_18_out, and_19_out, and_20_out, and_21_out, and_22_out, and_23_out, and_24_out, and_25_out,
       and_26_out, and_27_out, and_28_out, and_29_out, and_30_out, and_31_out, decoder_1_out_1,
       decoder_1_out_2, decoder_1_out_3, decoder_1_out_4, decoder_1_out_5, decoder_1_out_6, decoder_1_out_7,
       decoder_1_out_8, decoder_1_out_9, decoder_1_out_10, decoder_1_out_11, decoder_1_out_12,
       decoder_1_out_13, decoder_1_out_14, decoder_1_out_15, decoder_1_out_16, decoder_1_out_17,
       decoder_1_out_18, decoder_1_out_19, decoder_1_out_20, decoder_1_out_21, decoder_1_out_22,
       decoder_1_out_23, decoder_1_out_24, decoder_1_out_25, decoder_1_out_26, decoder_1_out_27,
       decoder_1_out_28, decoder_1_out_29, decoder_1_out_30, decoder_1_out_31;

  Decoder #(.Selector_Bits(5)) decoder_1 (
    .sel(WriteReg), .out_1(decoder_1_out_1), .out_2(decoder_1_out_2), .out_3(decoder_1_out_3),
    .out_4(decoder_1_out_4), .out_5(decoder_1_out_5), .out_6(decoder_1_out_6), .out_7(decoder_1_out_7),
    .out_8(decoder_1_out_8), .out_9(decoder_1_out_9), .out_10(decoder_1_out_10), .out_11(decoder_1_out_11),
    .out_12(decoder_1_out_12), .out_13(decoder_1_out_13), .out_14(decoder_1_out_14),
    .out_15(decoder_1_out_15), .out_16(decoder_1_out_16), .out_17(decoder_1_out_17),
    .out_18(decoder_1_out_18), .out_19(decoder_1_out_19), .out_20(decoder_1_out_20),
    .out_21(decoder_1_out_21), .out_22(decoder_1_out_22), .out_23(decoder_1_out_23),
    .out_24(decoder_1_out_24), .out_25(decoder_1_out_25), .out_26(decoder_1_out_26),
    .out_27(decoder_1_out_27), .out_28(decoder_1_out_28), .out_29(decoder_1_out_29),
    .out_30(decoder_1_out_30), .out_31(decoder_1_out_31));  // open: out_0
  and and_1 (and_1_out, WriteEn, decoder_1_out_1);
  and and_2 (and_2_out, WriteEn, decoder_1_out_2);
  and and_3 (and_3_out, WriteEn, decoder_1_out_3);
  and and_4 (and_4_out, WriteEn, decoder_1_out_4);
  and and_5 (and_5_out, WriteEn, decoder_1_out_5);
  and and_6 (and_6_out, WriteEn, decoder_1_out_6);
  and and_7 (and_7_out, WriteEn, decoder_1_out_7);
  and and_8 (and_8_out, WriteEn, decoder_1_out_8);
  and and_9 (and_9_out, WriteEn, decoder_1_out_9);
  and and_10 (and_10_out, WriteEn, decoder_1_out_10);
  and and_11 (and_11_out, WriteEn, decoder_1_out_11);
  and and_12 (and_12_out, WriteEn, decoder_1_out_12);
  and and_13 (and_13_out, WriteEn, decoder_1_out_13);
  and and_14 (and_14_out, WriteEn, decoder_1_out_14);
  and and_15 (and_15_out, WriteEn, decoder_1_out_15);
  and and_16 (and_16_out, WriteEn, decoder_1_out_16);
  and and_17 (and_17_out, WriteEn, decoder_1_out_17);
  and and_18 (and_18_out, WriteEn, decoder_1_out_18);
  and and_19 (and_19_out, WriteEn, decoder_1_out_19);
  and and_20 (and_20_out, WriteEn, decoder_1_out_20);
  and and_21 (and_21_out, WriteEn, decoder_1_out_21);
  and and_22 (and_22_out, WriteEn, decoder_1_out_22);
  and and_23 (and_23_out, WriteEn, decoder_1_out_23);
  and and_24 (and_24_out, WriteEn, decoder_1_out_24);
  and and_25 (and_25_out, WriteEn, decoder_1_out_25);
  and and_26 (and_26_out, WriteEn, decoder_1_out_26);
  and and_27 (and_27_out, WriteEn, decoder_1_out_27);
  and and_28 (and_28_out, WriteEn, decoder_1_out_28);
  and and_29 (and_29_out, WriteEn, decoder_1_out_29);
  and and_30 (and_30_out, WriteEn, decoder_1_out_30);
  and and_31 (and_31_out, WriteEn, decoder_1_out_31);
  _64_bit_register _64_bit_register_1 (.D(WriteData), .CLR(CLR), .EN(and_1_out), .CLK(CLK), .Q(x1));
  _64_bit_register _64_bit_register_2 (.D(WriteData), .CLR(CLR), .EN(and_2_out), .CLK(CLK), .Q(x2));
  _64_bit_register _64_bit_register_3 (.D(WriteData), .CLR(CLR), .EN(and_3_out), .CLK(CLK), .Q(x3));
  _64_bit_register _64_bit_register_4 (.D(WriteData), .CLR(CLR), .EN(and_4_out), .CLK(CLK), .Q(x4));
  _64_bit_register _64_bit_register_5 (.D(WriteData), .CLR(CLR), .EN(and_5_out), .CLK(CLK), .Q(x5));
  _64_bit_register _64_bit_register_6 (.D(WriteData), .CLR(CLR), .EN(and_6_out), .CLK(CLK), .Q(x6));
  _64_bit_register _64_bit_register_7 (.D(WriteData), .CLR(CLR), .EN(and_7_out), .CLK(CLK), .Q(x7));
  _64_bit_register _64_bit_register_8 (.D(WriteData), .CLR(CLR), .EN(and_8_out), .CLK(CLK), .Q(x8));
  _64_bit_register _64_bit_register_9 (.D(WriteData), .CLR(CLR), .EN(and_9_out), .CLK(CLK), .Q(x9));
  _64_bit_register _64_bit_register_10 (.D(WriteData), .CLR(CLR), .EN(and_10_out), .CLK(CLK), .Q(x10));
  _64_bit_register _64_bit_register_11 (.D(WriteData), .CLR(CLR), .EN(and_11_out), .CLK(CLK), .Q(x11));
  _64_bit_register _64_bit_register_12 (.D(WriteData), .CLR(CLR), .EN(and_12_out), .CLK(CLK), .Q(x12));
  _64_bit_register _64_bit_register_13 (.D(WriteData), .CLR(CLR), .EN(and_13_out), .CLK(CLK), .Q(x13));
  _64_bit_register _64_bit_register_14 (.D(WriteData), .CLR(CLR), .EN(and_14_out), .CLK(CLK), .Q(x14));
  _64_bit_register _64_bit_register_15 (.D(WriteData), .CLR(CLR), .EN(and_15_out), .CLK(CLK), .Q(x15));
  _64_bit_register _64_bit_register_16 (.D(WriteData), .CLR(CLR), .EN(and_16_out), .CLK(CLK), .Q(x16));
  _64_bit_register _64_bit_register_17 (.D(WriteData), .CLR(CLR), .EN(and_17_out), .CLK(CLK), .Q(x17));
  _64_bit_register _64_bit_register_18 (.D(WriteData), .CLR(CLR), .EN(and_18_out), .CLK(CLK), .Q(x18));
  _64_bit_register _64_bit_register_19 (.D(WriteData), .CLR(CLR), .EN(and_19_out), .CLK(CLK), .Q(x19));
  _64_bit_register _64_bit_register_20 (.D(WriteData), .CLR(CLR), .EN(and_20_out), .CLK(CLK), .Q(x20));
  _64_bit_register _64_bit_register_21 (.D(WriteData), .CLR(CLR), .EN(and_21_out), .CLK(CLK), .Q(x21));
  _64_bit_register _64_bit_register_22 (.D(WriteData), .CLR(CLR), .EN(and_22_out), .CLK(CLK), .Q(x22));
  _64_bit_register _64_bit_register_23 (.D(WriteData), .CLR(CLR), .EN(and_23_out), .CLK(CLK), .Q(x23));
  _64_bit_register _64_bit_register_24 (.D(WriteData), .CLR(CLR), .EN(and_24_out), .CLK(CLK), .Q(x24));
  _64_bit_register _64_bit_register_25 (.D(WriteData), .CLR(CLR), .EN(and_25_out), .CLK(CLK), .Q(x25));
  _64_bit_register _64_bit_register_26 (.D(WriteData), .CLR(CLR), .EN(and_26_out), .CLK(CLK), .Q(x26));
  _64_bit_register _64_bit_register_27 (.D(WriteData), .CLR(CLR), .EN(and_27_out), .CLK(CLK), .Q(x27));
  _64_bit_register _64_bit_register_28 (.D(WriteData), .CLR(CLR), .EN(and_28_out), .CLK(CLK), .Q(x28));
  _64_bit_register _64_bit_register_29 (.D(WriteData), .CLR(CLR), .EN(and_29_out), .CLK(CLK), .Q(x29));
  _64_bit_register _64_bit_register_30 (.D(WriteData), .CLR(CLR), .EN(and_30_out), .CLK(CLK), .Q(x30));
  _64_bit_register _64_bit_register_31 (.D(WriteData), .CLR(CLR), .EN(and_31_out), .CLK(CLK), .Q(x31));
  Multiplexer #(.Selector_Bits(5), .Bits(64)) multiplexer_1 (
    .sel(ReadReg1), .in_0({64{1'b0}}), .in_1(x1), .in_2(x2), .in_3(x3), .in_4(x4), .in_5(x5), .in_6(x6),
    .in_7(x7), .in_8(x8), .in_9(x9), .in_10(x10), .in_11(x11), .in_12(x12), .in_13(x13), .in_14(x14),
    .in_15(x15), .in_16(x16), .in_17(x17), .in_18(x18), .in_19(x19), .in_20(x20), .in_21(x21), .in_22(x22),
    .in_23(x23), .in_24(x24), .in_25(x25), .in_26(x26), .in_27(x27), .in_28(x28), .in_29(x29), .in_30(x30),
    .in_31(x31), .out(RD1));
  Multiplexer #(.Selector_Bits(5), .Bits(64)) multiplexer_2 (
    .sel(ReadReg0), .in_0({64{1'b0}}), .in_1(x1), .in_2(x2), .in_3(x3), .in_4(x4), .in_5(x5), .in_6(x6),
    .in_7(x7), .in_8(x8), .in_9(x9), .in_10(x10), .in_11(x11), .in_12(x12), .in_13(x13), .in_14(x14),
    .in_15(x15), .in_16(x16), .in_17(x17), .in_18(x18), .in_19(x19), .in_20(x20), .in_21(x21), .in_22(x22),
    .in_23(x23), .in_24(x24), .in_25(x25), .in_26(x26), .in_27(x27), .in_28(x28), .in_29(x29), .in_30(x30),
    .in_31(x31), .out(RD0));

  assign x0 = {64{1'b0}};
endmodule
